# Fritzing sketch DangerousEliteControl (saved by Fritzing 0.9.2b)
breadboards: 1

parts:
  Part1 = Arduino Leonardo (Rev3b)
  LED1 = LED - 5mm [color="Red (633nm)" package="5 mm [THT]"]
  LED2 = LED - 5mm [color="Blue (525nm)" package="5 mm [THT]"]
  R1 = Resistor [tolerance=±5% resistance=220 package=THT]
  S1 = Momentary Switch [package=ksa_sealed_tac_switch]
  S2 = Momentary Switch [package=ksa_sealed_tac_switch]
  R3 = Resistor [tolerance=±5% resistance=10k package=THT]
  R4 = Resistor [tolerance=±5% resistance=10k package=THT]
  S3 = Momentary Switch [package=ksa_sealed_tac_switch]
  U1 = Wiichuck Adapter
  R5 = Resistor [tolerance=±5% resistance=10k package=THT]

nets:
  N1: Part1.D4/A6, S1.4
  N2: Part1.D7, S2.4
  N3: Part1.5V, S1.1, S2.1, S3.1, U1.+
  N4: Part1.GND, R1.Pin_1, R3.Pin_1, R4.Pin_1, U1.-, R5.Pin_1
  N5: Part1.D8/A8, LED2.anode
  N6: Part1.D9_PWM/A9, S3.4
  N7: Part1.D10_PWM/A10, LED1.anode
  N8: Part1.SDA, U1.SDA
  N9: Part1.SCL, U1.SCL
  N10: LED1.cathode, LED2.cathode, R1.Pin_0
  N11: S1.3, R3.Pin_0
  N12: S2.3, R5.Pin_0
  N13: R4.Pin_0, S3.3

notes:
  In7 : Return Key
  In9 : Mode
  In 4 : Landing
  Out 8: Landing Mode
  Out 10: Combat Mode

custom parts:
  Wiichuck Adapter: SCP1000 Barometric Pressure sensor. Can sense air pressure and temperature. SPI interface.
